// Logisim project 2.70.circ as structural Verilog: 1 circuit, main circuit main
module main (
  input  A2,
  input  A1,
  input  A0,
  input  E,
  output B0,
  output B1,
  output B2,
  output B3,
  output B4,
  output B5,
  output B6,
  output B7
);

  wire not_1_out, not_2_out, not_3_out;

  not not_1 (not_1_out, A2);
  not not_2 (not_2_out, A1);
  not not_3 (not_3_out, A0);
  and and_1 (B0, not_1_out, not_2_out, not_3_out, E);
  and and_2 (B1, not_1_out, not_2_out, A0, E);
  and and_3 (B2, not_1_out, A1, not_3_out, E);
  and and_4 (B3, not_1_out, A1, A0, E);
  and and_5 (B4, A2, not_2_out, not_3_out, E);
  and and_6 (B5, A2, not_2_out, A0, E);
  and and_7 (B6, A2, A1, not_3_out, E);
  and and_8 (B7, A2, A1, A0, E);
endmodule
