// Logisim project 2.18.circ as structural Verilog: 3 circuits, main circuit a_2_18
module a_2_18 (
  input  a,
  input  b,
  input  c,
  output F
);

  wire and_1_out, and_2_out, not_1_out, not_2_out;

  not not_1 (not_1_out, b);
  not not_2 (not_2_out, a);
  and and_1 (and_1_out, not_2_out, not_1_out);
  and and_2 (and_2_out, not_1_out, c);
  or or_1 (F, and_1_out, and_2_out);
endmodule

module b_2_18 (
  input  a,
  input  b,
  input  c,
  input  d,
  input  e,
  output F
);

  wire and_1_out, and_2_out, and_3_out, and_4_out;

  and and_1 (and_1_out, a, b);
  and and_2 (and_2_out, b, c);
  and and_3 (and_3_out, c, d);
  and and_4 (and_4_out, d, e);
  or or_1 (F, and_1_out, and_2_out, and_3_out, and_4_out);
endmodule

module c_2_18 (
  input  a,
  input  b,
  input  c,
  input  d,
  input  e,
  input  f,
  output F0
);

  wire and_1_out, and_2_out, not_1_out, not_2_out, or_1_out, or_2_out;

  and and_1 (and_1_out, a, b);
  not not_1 (not_1_out, and_1_out);
  or or_1 (or_1_out, d, and_2_out);
  and and_2 (and_2_out, e, f);
  or or_2 (or_2_out, not_1_out, c);
  not not_2 (not_2_out, or_1_out);
  or or_3 (F0, or_2_out, not_2_out);
endmodule
