// Logisim project 3.40.circ as structural Verilog: 3 circuits, main circuit main
module main (
  input  a,
  input  b,
  output y
);

  wire clk_out, SequentialLogic_n0, SequentialLogic_n1, StateRegister_s0, StateRegister_s1;

  State StateRegister (
    .n0(SequentialLogic_n0), .n1(SequentialLogic_n1), .clk(clk_out), .s0(StateRegister_s0),
    .s1(StateRegister_s1));
  Logic SequentialLogic (
    .s1(StateRegister_s1), .s0(StateRegister_s0), .a(a), .b(b), .y(y), .n0(SequentialLogic_n0),
    .n1(SequentialLogic_n1));
  Clock clk (.out(clk_out));
endmodule

module State (
  input  n0,
  input  n1,
  input  clk,
  output s0,
  output s1
);

  and and_1 (s0, n0, clk);
  and and_2 (s1, n1, clk);
endmodule

module Logic (
  input  s1,
  input  s0,
  input  a,
  input  b,
  output y,
  output n0,
  output n1
);

  wire and_1_out, and_2_out, and_3_out, and_4_out, and_5_out, and_6_out, and_7_out, and_8_out, and_9_out,
       not_1_out, not_2_out, not_3_out, not_4_out;

  not not_1 (not_1_out, s1);
  not not_2 (not_2_out, s0);
  not not_3 (not_3_out, a);
  not not_4 (not_4_out, b);
  and and_1 (and_1_out, not_1_out, b);
  and and_2 (and_2_out, not_1_out, s0);
  and and_3 (and_3_out, s1, not_2_out, not_4_out);
  and and_4 (and_4_out, not_1_out, a, b);
  and and_5 (and_5_out, not_1_out, s0, a);
  and and_6 (and_6_out, s1, not_2_out);
  and and_7 (and_7_out, not_1_out, not_3_out, b);
  and and_8 (and_8_out, not_1_out, s0, not_3_out);
  and and_9 (and_9_out, s1, not_2_out, b);
  or or_1 (y, and_1_out, and_2_out, and_3_out);
  or or_2 (n0, and_4_out, and_5_out, and_6_out);
  or or_3 (n1, and_7_out, and_8_out, and_9_out);
endmodule
