// Logisim project 3.43.circ as structural Verilog: 3 circuits, main circuit main
module main (
  input  in_1,
  output out_2,
  output out_3,
  output out_4
);

  wire clock_1_out, SequentialLogic_n0, SequentialLogic_n1, SequentialLogic_n2, StateRegister_s0,
       StateRegister_s1, StateRegister_s2;

  StateReg StateRegister (
    .n2(SequentialLogic_n2), .n1(SequentialLogic_n1), .n0(SequentialLogic_n0), .clk(clock_1_out),
    .s2(StateRegister_s2), .s1(StateRegister_s1), .s0(StateRegister_s0));
  SeqLogic SequentialLogic (
    .s2(StateRegister_s2), .s1(StateRegister_s1), .s0(StateRegister_s0), .gnct(in_1), .x(out_2), .y(out_3),
    .z(out_4), .n2(SequentialLogic_n2), .n1(SequentialLogic_n1), .n0(SequentialLogic_n0));
  Clock clock_1 (.out(clock_1_out));
endmodule

module SeqLogic (
  input  s2,
  input  s1,
  input  s0,
  input  gnct,
  output x,
  output y,
  output z,
  output n2,
  output n1,
  output n0
);

  wire and_1_out, and_2_out, and_3_out, and_4_out, and_5_out, and_6_out, and_7_out, and_8_out, and_9_out,
       and_10_out, and_11_out, and_12_out, and_13_out, and_14_out, and_15_out, and_16_out, and_17_out,
       and_18_out, and_19_out, and_20_out, not_1_out, not_2_out, not_3_out, not_4_out;

  not not_1 (not_1_out, s2);
  not not_2 (not_2_out, s1);
  not not_3 (not_3_out, s0);
  not not_4 (not_4_out, gnct);
  and and_1 (and_1_out, not_1_out, s1, s0, gnct);
  and and_2 (and_2_out, s2, not_2_out);
  and and_3 (and_3_out, s2, not_3_out);
  and and_4 (and_4_out, s2, not_4_out);
  and and_5 (and_5_out, not_2_out, gnct);
  and and_6 (and_6_out, not_2_out, s0);
  and and_7 (and_7_out, s1, not_3_out, not_4_out);
  and and_8 (and_8_out, not_1_out, s0, gnct);
  and and_9 (and_9_out, not_1_out, s1);
  and and_10 (and_10_out, s2, not_2_out, not_3_out);
  and and_11 (and_11_out, s2, not_2_out, not_4_out);
  and and_12 (and_12_out, not_1_out, s1, s0, gnct);
  and and_13 (and_13_out, s2, not_2_out);
  and and_14 (and_14_out, s2, not_3_out);
  and and_15 (and_15_out, s2, not_4_out);
  and and_16 (and_16_out, not_2_out, s0, gnct);
  and and_17 (and_17_out, s1, not_3_out);
  and and_18 (and_18_out, s1, not_4_out);
  and and_19 (and_19_out, not_3_out, gnct);
  and and_20 (and_20_out, s0, not_4_out);
  or or_1 (x, and_1_out, and_2_out, and_3_out, and_4_out);
  or or_2 (y, and_5_out, and_6_out, and_7_out);
  or or_3 (z, and_8_out, and_9_out, and_10_out, and_11_out);
  or or_4 (n2, and_12_out, and_13_out, and_14_out, and_15_out);
  or or_5 (n1, and_16_out, and_17_out, and_18_out);
  or or_6 (n0, and_19_out, and_20_out);
endmodule

module StateReg (
  input  n2,
  input  n1,
  input  n0,
  input  clk,
  output s2,
  output s1,
  output s0
);

  and and_1 (s2, n2, clk);
  and and_2 (s1, n1, clk);
  and and_3 (s0, n0, clk);
endmodule
