// Logisim project 4.3.circ as structural Verilog: 1 circuit, main circuit main
module main (
  input  I3,
  input  I2,
  input  I1,
  input  I0,
  input  [1:0] s1s0,
  output Q3,
  output Q2,
  output Q1,
  output Q0
);

  wire multiplexer_1_out, multiplexer_2_out, multiplexer_3_out, multiplexer_4_out, not_1_out, not_2_out,
       not_3_out, not_4_out;

  not not_1 (not_1_out, Q3);
  Multiplexer #(.select(2)) multiplexer_1 (
    .in0(Q3), .in1(I3), .in2(1'b0), .in3(not_1_out), .out(multiplexer_1_out), .sel(s1s0));
  D_Flip_Flop d_ff_1 (.D(multiplexer_1_out), .Q(Q3));  // open: clk, Qn, preset, reset
  Multiplexer #(.select(2)) multiplexer_2 (
    .in0(Q2), .in1(I2), .in2(1'b0), .in3(not_2_out), .out(multiplexer_2_out), .sel(s1s0));
  D_Flip_Flop d_ff_2 (.D(multiplexer_2_out), .Q(Q2));  // open: clk, Qn, preset, reset
  not not_2 (not_2_out, Q2);
  Multiplexer #(.select(2)) multiplexer_3 (
    .in0(Q1), .in1(I1), .in2(1'b0), .in3(not_3_out), .out(multiplexer_3_out), .sel(s1s0));
  D_Flip_Flop d_ff_3 (.D(multiplexer_3_out), .Q(Q1));  // open: clk, Qn, preset, reset
  not not_3 (not_3_out, Q1);
  D_Flip_Flop d_ff_4 (.D(multiplexer_4_out), .Q(Q0));  // open: clk, Qn, preset, reset
  not not_4 (not_4_out, Q0);
  Multiplexer #(.select(2)) multiplexer_4 (
    .in0(Q0), .in1(I0), .in2(1'b0), .in3(not_4_out), .out(multiplexer_4_out), .sel(s1s0));
endmodule
