// Logisim project 4.40.circ as structural Verilog: 2 circuits, main circuit ALU
module ALU (
  input  [7:0] A,
  input  [7:0] B,
  input  x,
  input  y,
  input  z,
  output [7:0] S
);

  wire alextender_1_co;
  wire [7:0] alextender_1_a0, alextender_1_b0;

  ALExtender alextender_1 (
    .A(A), .B(B), .s2(x), .s1(y), .s0(z), .a0(alextender_1_a0), .b0(alextender_1_b0), .co(alextender_1_co));
  Adder adder_1 (.a(alextender_1_a0), .b(alextender_1_b0), .out(S), .cin(alextender_1_co));  // open: cout

  // Notes on the sheet:
  //   8-bit AL-Extender
  //   8-bit Adder
endmodule

module ALExtender (
  input  [7:0] A,
  input  [7:0] B,
  input  s2,
  input  s1,
  input  s0,
  output [7:0] a0,
  output [7:0] b0,
  output co
);
endmodule
