// Logisim project 4.62.circ as structural Verilog: 2 circuits, main circuit main
module main (
  input  [7:0] W_data,
  input  [1:0] W_addr,
  input  [1:0] R1_addr,
  input  W_en,
  input  R1_en,
  input  [1:0] R2_addr,
  input  R2_en,
  output [7:0] R1_data,
  output [7:0] R2_data
);

  wire clk_out, R1Decoder_d0, R1Decoder_d1, R1Decoder_d2, R1Decoder_d3, R2Decoder_d0, R2Decoder_d1,
       R2Decoder_d2, R2Decoder_d3, WriteDecoder_d0, WriteDecoder_d1, WriteDecoder_d2, WriteDecoder_d3;
  wire [7:0] buffer_1_out, controlled_buffer_1_out, controlled_buffer_2_out, controlled_buffer_3_out,
       controlled_buffer_4_out, controlled_buffer_5_out, controlled_buffer_6_out, controlled_buffer_7_out,
       controlled_buffer_8_out, register_1_q, register_2_q, register_3_q, register_4_q;

  Clock clk (.out(clk_out));
  Register register_1 (.D(W_data), .en(WriteDecoder_d0), .clk(clk_out), .Q(register_1_q));  // open: clr
  Decode WriteDecoder (
    .Addr(W_addr), .En(W_en), .d0(WriteDecoder_d0), .d1(WriteDecoder_d1), .d2(WriteDecoder_d2),
    .d3(WriteDecoder_d3));
  Register register_2 (.D(W_data), .en(WriteDecoder_d1), .clk(clk_out), .Q(register_2_q));  // open: clr
  assign buffer_1_out = W_data;  // Buffer buffer_1, 8 bits wide
  Register register_3 (.D(buffer_1_out), .en(WriteDecoder_d2), .clk(clk_out), .Q(register_3_q));  // open: clr
  Register register_4 (.D(buffer_1_out), .en(WriteDecoder_d3), .clk(clk_out), .Q(register_4_q));  // open: clr
  assign controlled_buffer_1_out = R1Decoder_d0 ? register_1_q : 8'bz;  // Controlled_Buffer controlled_buffer_1
  assign controlled_buffer_2_out = R1Decoder_d1 ? register_2_q : 8'bz;  // Controlled_Buffer controlled_buffer_2
  assign controlled_buffer_3_out = R2Decoder_d0 ? register_1_q : 8'bz;  // Controlled_Buffer controlled_buffer_3
  assign controlled_buffer_4_out = R2Decoder_d1 ? register_2_q : 8'bz;  // Controlled_Buffer controlled_buffer_4
  Decode R1Decoder (
    .Addr(R1_addr), .En(R1_en), .d0(R1Decoder_d0), .d1(R1Decoder_d1), .d2(R1Decoder_d2), .d3(R1Decoder_d3));
  assign controlled_buffer_5_out = R1Decoder_d2 ? register_3_q : 8'bz;  // Controlled_Buffer controlled_buffer_5
  assign controlled_buffer_6_out = R1Decoder_d3 ? register_4_q : 8'bz;  // Controlled_Buffer controlled_buffer_6
  Decode R2Decoder (
    .Addr(R2_addr), .En(R2_en), .d0(R2Decoder_d0), .d1(R2Decoder_d1), .d2(R2Decoder_d2), .d3(R2Decoder_d3));
  assign controlled_buffer_7_out = R2Decoder_d2 ? register_3_q : 8'bz;  // Controlled_Buffer controlled_buffer_7
  assign controlled_buffer_8_out = R2Decoder_d3 ? register_4_q : 8'bz;  // Controlled_Buffer controlled_buffer_8
  Multiplexer #(.enable("true"), .select(2), .width(8)) multiplexer_1 (
    .in0(controlled_buffer_1_out), .in1(controlled_buffer_2_out), .in2(controlled_buffer_5_out),
    .in3(controlled_buffer_6_out), .out(R1_data), .sel(R1_addr), .en(R1_en));
  Multiplexer #(.enable("true"), .select(2), .width(8)) multiplexer_2 (
    .in0(controlled_buffer_3_out), .in1(controlled_buffer_4_out), .in2(controlled_buffer_7_out),
    .in3(controlled_buffer_8_out), .out(R2_data), .sel(R2_addr), .en(R2_en));
endmodule

module Decode (
  input  [1:0] Addr,
  input  En,
  output d0,
  output d1,
  output d2,
  output d3
);

  wire not_1_out, not_2_out;

  not not_1 (not_1_out, Addr[1]);
  not not_2 (not_2_out, Addr[0]);
  and and_1 (d0, not_1_out, not_2_out, En);
  and and_2 (d1, not_1_out, Addr[0], En);
  and and_3 (d2, Addr[1], not_2_out, En);
  and and_4 (d3, Addr[1], Addr[0], En);
endmodule
