// Logisim project 4.13.circ as structural Verilog: 1 circuit, main circuit main
module main (
  input  [7:0] A,
  input  [7:0] B,
  input  [7:0] C,
  input  [7:0] D,
  output [7:0] S,
  output CO
);

  wire adder_1_cout, adder_2_cout, adder_3_cout;
  wire [7:0] adder_1_out, adder_2_out;

  Adder adder_1 (.a(A), .b(B), .out(adder_1_out), .cout(adder_1_cout));  // open: cin
  Adder adder_2 (.a(adder_1_out), .b(C), .out(adder_2_out), .cout(adder_2_cout));  // open: cin
  Adder adder_3 (.a(adder_2_out), .b(D), .out(S), .cout(adder_3_cout));  // open: cin
  ExactlyOne xor_1 (.out(CO), .in0(adder_1_cout), .in1(adder_2_cout), .in2(adder_3_cout));
endmodule
