// Logisim project 4.21.circ as structural Verilog: 1 circuit, main circuit main
module main (
  input  [15:0] A,
  input  [15:0] B,
  output [15:0] out_3
);

  wire comparator_1_lt;

  Multiplexer #(.width(16)) multiplexer_1 (.in0(A), .in1(B), .out(out_3), .sel(comparator_1_lt));
  Comparator #(.width(16)) comparator_1 (.a(A), .b(B), .lt(comparator_1_lt));  // open: gt, eq
endmodule
