// Logisim project Problem1.circ as structural Verilog: 2 circuits, main circuit F
module F (
);

  wire a_out, and_1_out, and_2_out, and_3_out, b_out, c_out, or_1_out, or_2_out, or_3_out, or_4_out;

  Button a (.out(a_out));
  Button b (.out(b_out));
  Button c (.out(c_out));
  and and_1 (and_1_out, a_out, b_out);
  and and_2 (and_2_out, a_out, b_out);
  or or_1 (or_1_out, a_out, b_out);
  and and_3 (and_3_out, and_1_out, c_out);
  or or_2 (or_2_out, or_1_out, c_out);
  or or_3 (or_3_out, and_3_out, and_2_out);
  or or_4 (or_4_out, or_3_out, or_2_out);
  LED F (.in(or_4_out));
endmodule

module G (
);

  wire a_out, and_1_out, and_2_out, and_3_out, and_4_out, and_5_out, and_6_out, b_out, c_out, not_1_out,
       not_2_out, not_3_out, or_1_out, or_2_out;

  Button a (.out(a_out));
  Button b (.out(b_out));
  Button c (.out(c_out));
  not not_1 (not_1_out, a_out);
  not not_2 (not_2_out, b_out);
  not not_3 (not_3_out, b_out);
  and and_1 (and_1_out, not_1_out, not_2_out);
  and and_2 (and_2_out, a_out, not_3_out);
  and and_3 (and_3_out, a_out, b_out);
  and and_4 (and_4_out, and_1_out, c_out);
  and and_5 (and_5_out, and_2_out, c_out);
  and and_6 (and_6_out, and_3_out, c_out);
  or or_1 (or_1_out, and_4_out, and_5_out);
  LED G (.in(or_2_out));
  or or_2 (or_2_out, or_1_out, and_6_out);
endmodule
