// Logisim project Problem2.circ as structural Verilog: 7 circuits, main circuit Decoder4x7
module main (
  input  C0,
  input  C1,
  input  C2,
  input  C3,
  input  C4,
  input  C5,
  input  C6
);

  wire ButtonIsPressed_a, ButtonIsPressed_b, ButtonIsPressed_c, ButtonIsPressed_d, ButtonIsPressed_e,
       ButtonIsPressed_f, ButtonIsPressed_g, Decoder_o_a, Decoder_o_b, Decoder_o_c, Decoder_o_d, Decoder_o_e,
       Decoder_o_f, Decoder_o_g, Encoder_a, Encoder_b, Encoder_c, onlyonebutton_1_f;

  Encoder7x3 Encoder (
    .s0(C0), .s1(C1), .s2(C2), .s3(C3), .s4(C4), .s5(C5), .S6(C6), .A(Encoder_a), .B(Encoder_b), .C(Encoder_c));
  OnlyOneButton onlyonebutton_1 (.C0(C0), .C1(C1), .C2(C2), .C3(C3), .C4(C4), .C5(C5), .C6(C6), .F(onlyonebutton_1_f));
  Decoder3x7 Decoder (
    .A(Encoder_a), .B(Encoder_b), .C(Encoder_c), .O_a(Decoder_o_a), .O_b(Decoder_o_b), .O_c(Decoder_o_c),
    .O_d(Decoder_o_d), .O_e(Decoder_o_e), .O_f(Decoder_o_f), .O_g(Decoder_o_g));
  HeptAND ButtonIsPressed (
    .i0(Decoder_o_a), .i1(Decoder_o_b), .i2(Decoder_o_c), .i3(Decoder_o_d), .i4(Decoder_o_e),
    .i5(Decoder_o_f), .i6(Decoder_o_g), .S(onlyonebutton_1_f), .a(ButtonIsPressed_a), .b(ButtonIsPressed_b),
    .c(ButtonIsPressed_c), .d(ButtonIsPressed_d), .e(ButtonIsPressed_e), .f(ButtonIsPressed_f),
    .g(ButtonIsPressed_g));
  _7_Segment_Display u_7_segment_display_1 (
    .g(ButtonIsPressed_g), .f(ButtonIsPressed_f), .a(ButtonIsPressed_a), .b(ButtonIsPressed_b),
    .e(ButtonIsPressed_e), .d(ButtonIsPressed_d), .c(ButtonIsPressed_c));  // open: dp
endmodule

module Decoder3x7 (
  input  A,
  input  B,
  input  C,
  output O_a,
  output O_b,
  output O_c,
  output O_d,
  output O_e,
  output O_f,
  output O_g
);

  wire and_1_out, and_2_out, and_3_out, and_4_out, and_5_out, and_6_out, and_7_out, and_8_out, and_9_out,
       and_10_out, and_11_out, and_12_out, and_13_out, and_14_out, and_15_out, and_16_out, not_1_out,
       not_2_out, not_3_out;

  not not_1 (not_1_out, A);
  not not_2 (not_2_out, B);
  not not_3 (not_3_out, C);
  and and_1 (and_1_out, not_1_out, not_3_out);
  or or_1 (O_a, and_1_out, B, and_2_out);
  and and_2 (and_2_out, A, C);
  and and_3 (and_3_out, not_2_out, not_3_out);
  or or_2 (O_b, not_1_out, and_3_out, and_4_out);
  and and_4 (and_4_out, B, C);
  or or_3 (O_c, not_2_out, C, A);
  and and_5 (and_5_out, not_1_out, not_3_out);
  and and_6 (and_6_out, not_1_out, B);
  and and_7 (and_7_out, B, not_3_out);
  and and_8 (and_8_out, A, not_2_out, C);
  and and_9 (and_9_out, not_1_out, not_3_out);
  or or_4 (O_e, and_9_out, and_10_out);
  and and_10 (and_10_out, B, not_3_out);
  and and_11 (and_11_out, not_2_out, not_3_out);
  and and_12 (and_12_out, A, not_2_out);
  or or_5 (O_f, and_11_out, and_12_out, and_13_out);
  and and_13 (and_13_out, A, not_3_out);
  and and_14 (and_14_out, not_1_out, B);
  and and_15 (and_15_out, A, not_2_out);
  or or_6 (O_g, and_14_out, and_15_out, and_16_out);
  and and_16 (and_16_out, A, not_3_out);
  or or_7 (O_d, and_5_out, and_6_out, and_7_out, and_8_out);
endmodule

module Decoder4x7 (
  input  A,
  input  B,
  input  C,
  input  D,
  output a0,
  output b0,
  output c0,
  output d0,
  output e0,
  output f0,
  output g0
);

  wire and_1_out, and_2_out, and_3_out, and_4_out, and_5_out, and_6_out, and_7_out, and_8_out, and_9_out,
       and_10_out, and_11_out, and_12_out, and_13_out, and_14_out, and_15_out, and_16_out, and_17_out,
       and_18_out, and_19_out, and_20_out, and_21_out, and_22_out, and_23_out, and_24_out, and_25_out,
       and_26_out, and_27_out, and_28_out, and_29_out, and_30_out, and_31_out, and_32_out, and_33_out,
       and_34_out, and_35_out, not_1_out, not_2_out, not_3_out, not_4_out, not_5_out, not_6_out, not_7_out,
       not_8_out, not_9_out, not_10_out, not_11_out, not_12_out, not_13_out, not_14_out, not_15_out,
       not_16_out, not_17_out, not_18_out, not_19_out, not_20_out, not_21_out, not_22_out, not_23_out,
       not_24_out, not_25_out, not_26_out, not_27_out, not_28_out, not_29_out, not_30_out, not_31_out,
       not_32_out, not_33_out, not_34_out, not_35_out, not_36_out, not_37_out, not_38_out, not_39_out,
       not_40_out, not_41_out, not_42_out, not_43_out, not_44_out;

  not not_1 (not_1_out, B);
  and and_1 (and_1_out, not_1_out, not_2_out);
  not not_2 (not_2_out, D);
  not not_3 (not_3_out, A);
  and and_2 (and_2_out, not_3_out, C);
  not not_4 (not_4_out, A);
  and and_3 (and_3_out, not_4_out, B, D);
  and and_4 (and_4_out, B, C);
  not not_5 (not_5_out, B);
  and and_5 (and_5_out, A, not_5_out, not_6_out);
  not not_6 (not_6_out, C);
  and and_6 (and_6_out, A, not_7_out);
  not not_7 (not_7_out, D);
  not not_8 (not_8_out, A);
  and and_7 (and_7_out, not_8_out, not_9_out);
  not not_9 (not_9_out, B);
  not not_10 (not_10_out, A);
  not not_11 (not_11_out, C);
  and and_8 (and_8_out, not_10_out, not_11_out, not_12_out);
  not not_12 (not_12_out, D);
  not not_13 (not_13_out, B);
  and and_9 (and_9_out, not_13_out, not_14_out);
  not not_14 (not_14_out, D);
  not not_15 (not_15_out, A);
  and and_10 (and_10_out, not_15_out, C, D);
  not not_16 (not_16_out, C);
  and and_11 (and_11_out, A, not_16_out, D);
  not not_17 (not_17_out, A);
  and and_12 (and_12_out, not_17_out, not_18_out);
  not not_18 (not_18_out, C);
  not not_19 (not_19_out, A);
  and and_13 (and_13_out, not_19_out, D);
  not not_20 (not_20_out, C);
  and and_14 (and_14_out, not_20_out, D);
  not not_21 (not_21_out, A);
  and and_15 (and_15_out, not_21_out, B);
  and and_16 (and_16_out, A, not_22_out);
  not not_22 (not_22_out, B);
  not not_23 (not_23_out, A);
  not not_24 (not_24_out, B);
  and and_17 (and_17_out, not_23_out, not_24_out, not_25_out);
  not not_25 (not_25_out, D);
  not not_26 (not_26_out, B);
  and and_18 (and_18_out, not_26_out, C, D);
  not not_27 (not_27_out, C);
  and and_19 (and_19_out, B, not_27_out, D);
  and and_20 (and_20_out, B, C, not_28_out);
  not not_28 (not_28_out, D);
  not not_29 (not_29_out, C);
  and and_21 (and_21_out, A, not_29_out, not_30_out);
  not not_30 (not_30_out, D);
  not not_31 (not_31_out, B);
  and and_22 (and_22_out, not_31_out, not_32_out);
  not not_32 (not_32_out, D);
  and and_23 (and_23_out, C, not_33_out);
  not not_33 (not_33_out, D);
  and and_24 (and_24_out, A, C);
  and and_25 (and_25_out, A, B);
  not not_34 (not_34_out, C);
  and and_26 (and_26_out, not_34_out, not_35_out);
  not not_35 (not_35_out, D);
  not not_36 (not_36_out, A);
  and and_27 (and_27_out, not_36_out, B, not_37_out);
  not not_37 (not_37_out, C);
  and and_28 (and_28_out, B, not_38_out);
  not not_38 (not_38_out, D);
  and and_29 (and_29_out, A, not_39_out);
  not not_39 (not_39_out, B);
  and and_30 (and_30_out, A, C);
  not not_40 (not_40_out, B);
  and and_31 (and_31_out, not_40_out, C);
  and and_32 (and_32_out, C, not_41_out);
  not not_41 (not_41_out, D);
  not not_42 (not_42_out, A);
  and and_33 (and_33_out, not_42_out, B, not_43_out);
  not not_43 (not_43_out, C);
  and and_34 (and_34_out, A, not_44_out);
  not not_44 (not_44_out, B);
  and and_35 (and_35_out, A, D);
  or or_1 (b0, and_7_out, and_8_out, and_9_out, and_10_out, and_11_out);
  or or_2 (c0, and_12_out, and_13_out, and_14_out, and_15_out, and_16_out);
  or or_3 (d0, and_17_out, and_18_out, and_19_out, and_20_out, and_21_out);
  or or_4 (e0, and_22_out, and_23_out, and_24_out, and_25_out);
  or or_5 (f0, and_26_out, and_27_out, and_28_out, and_29_out, and_30_out);
  or or_6 (g0, and_31_out, and_32_out, and_33_out, and_34_out, and_35_out);
  or or_7 (a0, and_1_out, and_2_out, and_3_out, and_4_out, and_5_out, and_6_out);
endmodule

module Encoder7x3 (
  input  s0,
  input  s1,
  input  s2,
  input  s3,
  input  s4,
  input  s5,
  input  S6,
  output A,
  output B,
  output C
);

  or or_1 (A, s4, S6, s5);
  or or_2 (B, s2, S6, s3);
  or or_3 (C, s1, s3, s5);
endmodule

module Encoder16x4 (
  input  y0,
  input  y1,
  input  y2,
  input  y3,
  input  y4,
  input  y5,
  input  y6,
  input  y7,
  input  y8,
  input  y9,
  input  yA,
  input  yB,
  input  yC,
  input  yD,
  input  yE,
  input  yF,
  output A,
  output B,
  output C,
  output D
);

  or or_1 (A, y8, y9, yA, yB, yC, yD, yE, yF);
  or or_2 (B, y4, y5, y6, y7, yC, yD, yE, yF);
  or or_3 (C, y2, y3, y6, y7, yA, yB, yE, yF);
  or or_4 (D, y1, y3, y5, y7, y9, yB, yD, yF);
endmodule

module HeptAND (
  input  i0,
  input  i1,
  input  i2,
  input  i3,
  input  i4,
  input  i5,
  input  i6,
  input  S,
  output a,
  output b,
  output c,
  output d,
  output e,
  output f,
  output g
);

  and and_1 (a, i0, S);
  and and_2 (b, i1, S);
  and and_3 (c, i2, S);
  and and_4 (d, i3, S);
  and and_5 (e, i4, S);
  and and_6 (f, i5, S);
  and and_7 (g, i6, S);
endmodule

module OnlyOneButton (
  input  C0,
  input  C1,
  input  C2,
  input  C3,
  input  C4,
  input  C5,
  input  C6,
  output F
);

  wire or_1_out, xor_1_out;

  or or_1 (or_1_out, C0, C1, C2, C6, C3, C4, C5);
  ExactlyOne xor_1 (.out(xor_1_out), .in0(C0), .in1(C1), .in2(C2), .in3(C6), .in4(C3), .in5(C4), .in6(C5));
  and and_1 (F, or_1_out, xor_1_out);
endmodule
