// Logisim project Problem2.circ as structural Verilog: 2 circuits, main circuit main
module main (
);

  wire button_1_out, clock_1_out, d_ff_1_q, d_ff_2_q, logic_1_n0, logic_1_n1, logic_1_o;

  Clock clock_1 (.out(clock_1_out));
  Button button_1 (.out(button_1_out));
  D_Flip_Flop d_ff_1 (.D(logic_1_n1), .clk(clock_1_out), .Q(d_ff_1_q));  // open: Qn, preset, reset
  D_Flip_Flop d_ff_2 (.D(logic_1_n0), .clk(clock_1_out), .Q(d_ff_2_q));  // open: Qn, preset, reset
  Logic logic_1 (.s1(d_ff_1_q), .s0(d_ff_2_q), .T(button_1_out), .n1(logic_1_n1), .n0(logic_1_n0), .O(logic_1_o));
  LED led_1 (.in(logic_1_o));

  // Notes on the sheet:
  //   74x74 pins 1-6
  //   74x74 pins 8-13
endmodule

module Logic (
  input  s1,
  input  s0,
  input  T,
  output n1,
  output n0,
  output O
);

  wire and_1_out, and_2_out, and_3_out, and_4_out, and_5_out, and_6_out, not_1_out, not_2_out, not_3_out;

  not not_1 (not_1_out, s1);
  not not_2 (not_2_out, s0);
  not not_3 (not_3_out, T);
  and and_1 (and_1_out, not_1_out, s0, not_3_out);
  and and_2 (and_2_out, s1, not_2_out);
  and and_3 (and_3_out, s1, T);
  and and_4 (and_4_out, not_1_out, T);
  and and_5 (and_5_out, not_1_out, s0);
  and and_6 (and_6_out, s1, not_2_out, not_3_out);
  or or_1 (n1, and_1_out, and_2_out, and_3_out);
  or or_2 (O, and_4_out, and_5_out, and_6_out);

  assign n0 = T;

  // Notes on the sheet:
  //   74x04 pins 1-2
  //   74x04 pins 3-4
  //   74x04 pins 5-6
  //   74x08 pin 1-3
  //   74x08 pin 4-6
  //   74x11 pins 1,2,13,14
  //   74x08 pin 8-10
  //   74x08 pin 11-13
  //   74x11 pins 3-6
endmodule
