// Logisim project Problem2.circ as structural Verilog: 2 circuits, main circuit main
module main (
  input  B,
  output O
);

  wire clock_1_out, d_ff_1_q, d_ff_2_q, FSM_n1, FSM_n2, not_1_out, not_2_out;

  Clock clock_1 (.out(clock_1_out));
  D_Flip_Flop d_ff_1 (.clk(clock_1_out), .Q(d_ff_1_q), .preset(FSM_n1), .reset(not_1_out));  // open: D, Qn
  D_Flip_Flop d_ff_2 (.clk(clock_1_out), .Q(d_ff_2_q), .preset(FSM_n2), .reset(not_2_out));  // open: D, Qn
  not not_1 (not_1_out, FSM_n1);
  not not_2 (not_2_out, FSM_n2);
  Logic FSM (.s1(d_ff_1_q), .s0(d_ff_2_q), .clk(clock_1_out), .B(B), .n1(FSM_n1), .n2(FSM_n2), .O(O));
endmodule

module Logic (
  input  s1,
  input  s0,
  input  clk,
  input  B,
  output n1,
  output n2,
  output O
);

  wire and_1_out, and_2_out, and_3_out;

  and and_1 (and_1_out, s1, clk);
  and and_2 (and_2_out, s0, clk);
  and and_3 (and_3_out, B, clk);
endmodule
