// Logisim project Problem3.circ as structural Verilog: 4 circuits, main circuit main
module main (
  input  A3,
  input  A2,
  input  A1,
  input  A0,
  input  E
);

  wire clock_1_out, logic_1_ac, logic_1_d0, logic_1_d1, logic_1_d2, logic_1_d3, logic_1_engine,
       logic_1_wipers, stateregister_1_o0, stateregister_1_o1, stateregister_1_o2, stateregister_1_o3,
       stateregister_1_o4, stateregister_1_o5, stateregister_1_o6;

  Logic logic_1 (
    .A3(A3), .A2(A2), .A1(A1), .A0(A0), .IOEnable(E), .AC(logic_1_ac), .D0(logic_1_d0), .D1(logic_1_d1),
    .D2(logic_1_d2), .D3(logic_1_d3), .Engine(logic_1_engine), .Wipers(logic_1_wipers));
  Clock clock_1 (.out(clock_1_out));
  LedBar #(.matrixcols(7)) ledbar_1 (
    .led0(stateregister_1_o0), .led1(stateregister_1_o1), .led2(stateregister_1_o2),
    .led3(stateregister_1_o3), .led4(stateregister_1_o4), .led5(stateregister_1_o5), .led6(stateregister_1_o6));
  StateRegister stateregister_1 (
    .AC(logic_1_ac), .D0(logic_1_d0), .D1(logic_1_d1), .D2(logic_1_d2), .D3(logic_1_d3),
    .Engine(logic_1_engine), .Wiper(logic_1_wipers), .clk(clock_1_out), .A3(A3), .A2(A2), .A1(A1), .A0(A0),
    .E(E), .O0(stateregister_1_o0), .O1(stateregister_1_o1), .O2(stateregister_1_o2),
    .O3(stateregister_1_o3), .O4(stateregister_1_o4), .O5(stateregister_1_o5), .O6(stateregister_1_o6));
endmodule

module Logic (
  input  A3,
  input  A2,
  input  A1,
  input  A0,
  input  IOEnable,
  output AC,
  output D0,
  output D1,
  output D2,
  output D3,
  output Engine,
  output Wipers
);

  wire not_1_out, not_2_out, not_3_out, not_4_out;

  not not_1 (not_1_out, A3);
  not not_2 (not_2_out, A2);
  not not_3 (not_3_out, A1);
  not not_4 (not_4_out, A0);
  and and_1 (AC, not_1_out, not_2_out, not_3_out, not_4_out, IOEnable);
  and and_2 (D0, not_1_out, not_2_out, not_3_out, A0, IOEnable);
  and and_3 (D1, not_1_out, not_2_out, A1, not_4_out, IOEnable);
  and and_4 (D2, not_1_out, not_2_out, A1, A0, IOEnable);
  and and_5 (D3, not_1_out, A2, not_3_out, not_4_out, IOEnable);
  and and_6 (Engine, not_1_out, A2, not_3_out, A0, IOEnable);
  and and_7 (Wipers, not_1_out, A2, A1, not_4_out, IOEnable);
endmodule

module StateRegister (
  input  AC,
  input  D0,
  input  D1,
  input  D2,
  input  D3,
  input  Engine,
  input  Wiper,
  input  clk,
  input  A3,
  input  A2,
  input  A1,
  input  A0,
  input  E,
  output O0,
  output O1,
  output O2,
  output O3,
  output O4,
  output O5,
  output O6
);

  wire and_1_out, and_2_out, and_3_out, and_4_out, decode_1_o0, decode_1_o1, decode_1_o2, decode_1_o3,
       decode_1_o4, decode_1_o5, decode_1_o6, decode_2_o0, decode_2_o1, decode_2_o2, decode_2_o3,
       decode_2_o4, decode_2_o5, decode_2_o6;

  and and_1 (and_1_out, A3, A2);
  and and_2 (and_2_out, A3, A1);
  and and_3 (and_3_out, A3, A0);
  and and_4 (and_4_out, A3, E);
  Decode decode_1 (
    .A2(and_1_out), .A1(and_2_out), .A0(and_3_out), .E(and_4_out), .O0(decode_1_o0), .O1(decode_1_o1),
    .O2(decode_1_o2), .O3(decode_1_o3), .O4(decode_1_o4), .O5(decode_1_o5), .O6(decode_1_o6));
  Decode decode_2 (
    .A2(A2), .A1(A1), .A0(A0), .E(E), .O0(decode_2_o0), .O1(decode_2_o1), .O2(decode_2_o2), .O3(decode_2_o3),
    .O4(decode_2_o4), .O5(decode_2_o5), .O6(decode_2_o6));
  Register #(.width(1)) register_1 (.D(AC), .en(decode_2_o0), .clk(clk), .Q(O0), .clr(decode_1_o0));
  Register #(.width(1)) register_2 (.D(D0), .en(decode_2_o1), .clk(clk), .Q(O1), .clr(decode_1_o1));
  Register #(.width(1)) register_3 (.D(D1), .en(decode_2_o2), .clk(clk), .Q(O2), .clr(decode_1_o2));
  Register #(.width(1)) register_4 (.D(D2), .en(decode_2_o3), .clk(clk), .Q(O3), .clr(decode_1_o3));
  Register #(.width(1)) register_5 (.D(D3), .en(decode_2_o4), .clk(clk), .Q(O4), .clr(decode_1_o4));
  Register #(.width(1)) register_6 (.D(Engine), .en(decode_2_o5), .clk(clk), .Q(O5), .clr(decode_1_o5));
  Register #(.width(1)) register_7 (.D(Wiper), .en(decode_2_o6), .clk(clk), .Q(O6), .clr(decode_1_o6));
endmodule

module Decode (
  input  A2,
  input  A1,
  input  A0,
  input  E,
  output O0,
  output O1,
  output O2,
  output O3,
  output O4,
  output O5,
  output O6
);

  wire not_1_out, not_2_out, not_3_out;

  not not_1 (not_1_out, A2);
  not not_2 (not_2_out, A1);
  not not_3 (not_3_out, A0);
  and and_1 (O0, not_1_out, not_2_out, not_3_out, E);
  and and_2 (O1, not_1_out, not_2_out, A0, E);
  and and_3 (O2, not_1_out, A1, not_3_out, E);
  and and_4 (O3, not_1_out, A1, A0, E);
  and and_5 (O4, A2, not_2_out, not_3_out, E);
  and and_6 (O5, A2, not_2_out, A0, E);
  and and_7 (O6, A2, A1, not_3_out, E);
endmodule
