// Logisim project Problem1.circ as structural Verilog: 3 circuits, main circuit main
module main (
  input  [7:0] addr,
  input  [2:0] ControlSignal,
  input  [7:0] Store,
  output [7:0] O0,
  output [7:0] O1,
  output [7:0] O2,
  output [7:0] O3,
  output [7:0] Load
);

  wire clk_out, decode_1_o_0, decode_1_o_1, decode_1_o_2, decode_1_o_3, decode_1_o_4;
  wire [7:0] controlled_buffer_4_out, iocontroller_1_busout, RandomAccessMemory_data, ReadOnlyMemory_data;

  Clock clk (.out(clk_out));
  ROM ReadOnlyMemory (.addr(addr), .data(ReadOnlyMemory_data));
  Decode decode_1 (
    .ControlSig(ControlSignal), .O_0(decode_1_o_0), .O_1(decode_1_o_1), .O_2(decode_1_o_2),
    .O_3(decode_1_o_3), .O_4(decode_1_o_4));
  assign Load = decode_1_o_0 ? ReadOnlyMemory_data : 8'bz;  // Controlled_Buffer controlled_buffer_1
  RAM #(.databus("bidir")) RandomAccessMemory (
    .addr(addr), .we(decode_1_o_2), .oe(decode_1_o_1), .clk(clk_out), .data(RandomAccessMemory_data));
  assign Load = decode_1_o_1 ? RandomAccessMemory_data : 8'bz;  // Controlled_Buffer controlled_buffer_2
  assign RandomAccessMemory_data = decode_1_o_2 ? Store : 8'bz;  // Controlled_Buffer controlled_buffer_3
  assign controlled_buffer_4_out = decode_1_o_4 ? Store : 8'bz;  // Controlled_Buffer controlled_buffer_4
  IOController iocontroller_1 (
    .clk(clk_out), .Enable(decode_1_o_4), .addr(addr), .BusIN(controlled_buffer_4_out), .O_0(O0), .O_1(O1),
    .O_2(O2), .O_3(O3), .BusOUT(iocontroller_1_busout));
  assign Load = decode_1_o_3 ? iocontroller_1_busout : 8'bz;  // Controlled_Buffer controlled_buffer_5

  // Notes on the sheet:
  //   000 Read from ROM
  //   001 Read from RAM
  //   010 Write to RAM
  //   011 Read from IO
  //   100 Write to IO
  //   contents of ReadOnlyMemory (hex, n*v repeats v):
  //   34 25 f4 86
endmodule

module IOController (
  input  clk,
  input  Enable,
  input  [7:0] addr,
  input  [7:0] BusIN,
  output [7:0] O_0,
  output [7:0] O_1,
  output [7:0] O_2,
  output [7:0] O_3,
  output [7:0] BusOUT
);

  wire demultiplexer_1_out0, demultiplexer_1_out1, demultiplexer_1_out2, demultiplexer_1_out3;
  wire [7:0] controlled_buffer_1_out, controlled_buffer_2_out, controlled_buffer_3_out,
       controlled_buffer_4_out, demultiplexer_2_out0, demultiplexer_2_out1, demultiplexer_2_out2,
       demultiplexer_2_out3;

  Demultiplexer #(.select(2)) demultiplexer_1 (
    .out0(demultiplexer_1_out0), .out1(demultiplexer_1_out1), .out2(demultiplexer_1_out2),
    .out3(demultiplexer_1_out3), .in(Enable), .sel(addr[1:0]));
  Demultiplexer #(.select(2), .width(8)) demultiplexer_2 (
    .out0(demultiplexer_2_out0), .out1(demultiplexer_2_out1), .out2(demultiplexer_2_out2),
    .out3(demultiplexer_2_out3), .in(BusIN), .sel(addr[1:0]));
  Register register_1 (.D(controlled_buffer_1_out), .en(demultiplexer_1_out0), .clk(clk), .Q(O_0));  // open: clr
  assign controlled_buffer_1_out = demultiplexer_1_out0 ? demultiplexer_2_out0 : 8'bz;  // Controlled_Buffer controlled_buffer_1
  assign controlled_buffer_2_out = demultiplexer_1_out1 ? demultiplexer_2_out1 : 8'bz;  // Controlled_Buffer controlled_buffer_2
  Register register_2 (.D(controlled_buffer_2_out), .en(demultiplexer_1_out1), .clk(clk), .Q(O_1));  // open: clr
  Register register_3 (.D(controlled_buffer_3_out), .en(demultiplexer_1_out2), .clk(clk), .Q(O_2));  // open: clr
  assign controlled_buffer_3_out = demultiplexer_1_out2 ? demultiplexer_2_out2 : 8'bz;  // Controlled_Buffer controlled_buffer_3
  Register register_4 (.D(controlled_buffer_4_out), .en(demultiplexer_1_out3), .clk(clk), .Q(O_3));  // open: clr
  assign controlled_buffer_4_out = demultiplexer_1_out3 ? demultiplexer_2_out3 : 8'bz;  // Controlled_Buffer controlled_buffer_4
  Multiplexer #(.select(2), .width(8)) multiplexer_1 (
    .in0(O_0), .in1(O_1), .in2(O_2), .in3(O_3), .out(BusOUT), .sel(addr[1:0]));
endmodule

module Decode (
  input  [2:0] ControlSig,
  output O_0,
  output O_1,
  output O_2,
  output O_3,
  output O_4
);

  wire not_1_out, not_2_out, not_3_out;

  not not_1 (not_1_out, ControlSig[2]);
  not not_2 (not_2_out, ControlSig[1]);
  not not_3 (not_3_out, ControlSig[0]);
  and and_1 (O_0, not_1_out, not_2_out, not_3_out);
  and and_2 (O_1, not_1_out, not_2_out, ControlSig[0]);
  and and_3 (O_2, not_1_out, ControlSig[1], not_3_out);
  and and_4 (O_3, not_1_out, ControlSig[1], ControlSig[0]);
  and and_5 (O_4, ControlSig[2], not_2_out, not_3_out);
endmodule
