// Logisim project Problem2.circ as structural Verilog: 11 circuits, main circuit main
module main (
  input  [7:0] in_1,
  input  [7:0] in_2,
  input  in_3,
  input  [7:0] in_4,
  input  [7:0] in_5,
  input  in_6,
  input  [7:0] in_7,
  input  [7:0] in_8,
  input  in_9,
  input  [7:0] in_10,
  input  [7:0] in_11,
  input  [7:0] in_12,
  input  [7:0] in_13,
  input  [7:0] in_14,
  input  [7:0] in_15,
  output out_16,
  output [7:0] out_17,
  output out_18,
  output [7:0] out_19,
  output out_20,
  output [7:0] out_21,
  output [7:0] out_22,
  output [7:0] out_23,
  output [7:0] out_24
);

  EightBitAdder eightbitadder_1 (.A(in_1), .B(in_2), .Ci(in_3), .Co(out_16), .S(out_17));
  EightBitAdder eightbitadder_2 (.A(in_4), .B(in_5), .Ci(in_6), .Co(out_18), .S(out_19));
  EightBitAdder eightbitadder_3 (.A(in_7), .B(in_8), .Ci(in_9), .Co(out_20), .S(out_21));
  EightBitSubtractor eightbitsubtractor_1 (.in_1(in_10), .in_2(in_11), .out_3(out_22));
  EightBitSubtractor eightbitsubtractor_2 (.in_1(in_12), .in_2(in_13), .out_3(out_23));
  EightBitSubtractor eightbitsubtractor_3 (.in_1(in_14), .in_2(in_15), .out_3(out_24));
endmodule

module SingleBitAdder (
  input  A,
  input  B,
  input  Ci,
  output Co,
  output S
);

  wire and_1_out, and_2_out, and_3_out;

  and and_1 (and_1_out, A, B);
  and and_2 (and_2_out, A, Ci);
  and and_3 (and_3_out, B, Ci);
  or or_1 (Co, and_1_out, and_2_out, and_3_out);
  xor xor_1 (S, A, B, Ci);
endmodule

module EightBitAdder (
  input  [7:0] A,
  input  [7:0] B,
  input  Ci,
  output Co,
  output [7:0] S
);

  wire singlebitadder_1_co, singlebitadder_2_co, singlebitadder_3_co, singlebitadder_4_co,
       singlebitadder_5_co, singlebitadder_6_co, singlebitadder_7_co;

  SingleBitAdder singlebitadder_1 (.A(A[0]), .B(B[0]), .Ci(Ci), .Co(singlebitadder_1_co), .S(S[0]));
  SingleBitAdder singlebitadder_2 (.A(A[1]), .B(B[1]), .Ci(singlebitadder_1_co), .Co(singlebitadder_2_co), .S(S[1]));
  SingleBitAdder singlebitadder_3 (.A(A[2]), .B(B[2]), .Ci(singlebitadder_2_co), .Co(singlebitadder_3_co), .S(S[2]));
  SingleBitAdder singlebitadder_4 (.A(A[3]), .B(B[3]), .Ci(singlebitadder_3_co), .Co(singlebitadder_4_co), .S(S[3]));
  SingleBitAdder singlebitadder_5 (.A(A[4]), .B(B[4]), .Ci(singlebitadder_4_co), .Co(singlebitadder_5_co), .S(S[4]));
  SingleBitAdder singlebitadder_6 (.A(A[5]), .B(B[5]), .Ci(singlebitadder_5_co), .Co(singlebitadder_6_co), .S(S[5]));
  SingleBitAdder singlebitadder_7 (.A(A[6]), .B(B[6]), .Ci(singlebitadder_6_co), .Co(singlebitadder_7_co), .S(S[6]));
  SingleBitAdder singlebitadder_8 (.A(A[7]), .B(B[7]), .Ci(singlebitadder_7_co), .Co(Co), .S(S[7]));
endmodule

module EightBitSubtractor (
  input  [7:0] in_1,
  input  [7:0] in_2,
  output [7:0] out_3
);

  wire eightbitadder_1_co;
  wire [7:0] not_1_out;

  assign not_1_out = ~in_2;  // NOT_Gate not_1, 8 bits wide
  EightBitAdder eightbitadder_1 (.A(in_1), .B(not_1_out), .Ci(1'b1), .Co(eightbitadder_1_co), .S(out_3));
endmodule

module L1 (
  input  [7:0] A,
  input  Shift,
  output [7:0] O
);

  Multiplexer multiplexer_1 (.in0(A[7]), .in1(A[6]), .out(O[7]), .sel(Shift));
  Multiplexer multiplexer_2 (.in0(A[6]), .in1(A[5]), .out(O[6]), .sel(Shift));
  Multiplexer multiplexer_3 (.in0(A[5]), .in1(A[4]), .out(O[5]), .sel(Shift));
  Multiplexer multiplexer_4 (.in0(A[4]), .in1(A[3]), .out(O[4]), .sel(Shift));
  Multiplexer multiplexer_5 (.in0(A[3]), .in1(A[2]), .out(O[3]), .sel(Shift));
  Multiplexer multiplexer_6 (.in0(A[2]), .in1(A[1]), .out(O[2]), .sel(Shift));
  Multiplexer multiplexer_7 (.in0(A[1]), .in1(A[0]), .out(O[1]), .sel(Shift));
  Multiplexer multiplexer_8 (.in0(A[0]), .in1(1'b0), .out(O[0]), .sel(Shift));
endmodule

module LeftShift (
  input  [7:0] A,
  input  [2:0] Shift,
  output [7:0] O
);

  wire decode_1_o1, decode_1_o2, decode_1_o3, decode_1_o4, decode_1_o5, decode_1_o6, decode_1_o7;
  wire [7:0] l1_1_o, l1_2_o, l1_3_o, l1_4_o, l1_5_o, l1_6_o;

  Decode decode_1 (
    .Shift(Shift), .O1(decode_1_o1), .O2(decode_1_o2), .O3(decode_1_o3), .O4(decode_1_o4), .O5(decode_1_o5),
    .O6(decode_1_o6), .O7(decode_1_o7));
  L1 l1_1 (.A(A), .Shift(decode_1_o1), .O(l1_1_o));
  L1 l1_2 (.A(l1_1_o), .Shift(decode_1_o2), .O(l1_2_o));
  L1 l1_3 (.A(l1_2_o), .Shift(decode_1_o3), .O(l1_3_o));
  L1 l1_4 (.A(l1_3_o), .Shift(decode_1_o4), .O(l1_4_o));
  L1 l1_5 (.A(l1_4_o), .Shift(decode_1_o5), .O(l1_5_o));
  L1 l1_6 (.A(l1_5_o), .Shift(decode_1_o6), .O(l1_6_o));
  L1 l1_7 (.A(l1_6_o), .Shift(decode_1_o7), .O(O));
endmodule

module R1 (
  input  [7:0] A,
  input  Arithmetic,
  input  Shift,
  output [7:0] O
);

  wire not_1_out, or_1_out;

  or or_1 (or_1_out, Arithmetic, not_1_out);
  not not_1 (not_1_out, Shift);
  Multiplexer multiplexer_1 (.in0(1'b0), .in1(A[7]), .out(O[7]), .sel(or_1_out));
  Multiplexer multiplexer_2 (.in0(A[6]), .in1(A[7]), .out(O[6]), .sel(Shift));
  Multiplexer multiplexer_3 (.in0(A[5]), .in1(A[6]), .out(O[5]), .sel(Shift));
  Multiplexer multiplexer_4 (.in0(A[4]), .in1(A[5]), .out(O[4]), .sel(Shift));
  Multiplexer multiplexer_5 (.in0(A[3]), .in1(A[4]), .out(O[3]), .sel(Shift));
  Multiplexer multiplexer_6 (.in0(A[2]), .in1(A[3]), .out(O[2]), .sel(Shift));
  Multiplexer multiplexer_7 (.in0(A[1]), .in1(A[2]), .out(O[1]), .sel(Shift));
  Multiplexer multiplexer_8 (.in0(A[0]), .in1(A[1]), .out(O[0]), .sel(Shift));
endmodule

module RightShift (
  input  [7:0] A,
  input  Arithmetic,
  input  [2:0] Shift,
  output [7:0] O
);

  wire decode_1_o1, decode_1_o2, decode_1_o3, decode_1_o4, decode_1_o5, decode_1_o6, decode_1_o7;
  wire [7:0] r1_1_o, r1_2_o, r1_3_o, r1_4_o, r1_5_o, r1_6_o;

  Decode decode_1 (
    .Shift(Shift), .O1(decode_1_o1), .O2(decode_1_o2), .O3(decode_1_o3), .O4(decode_1_o4), .O5(decode_1_o5),
    .O6(decode_1_o6), .O7(decode_1_o7));
  R1 r1_1 (.A(A), .Arithmetic(Arithmetic), .Shift(decode_1_o1), .O(r1_1_o));
  R1 r1_2 (.A(r1_1_o), .Arithmetic(Arithmetic), .Shift(decode_1_o2), .O(r1_2_o));
  R1 r1_3 (.A(r1_2_o), .Arithmetic(Arithmetic), .Shift(decode_1_o3), .O(r1_3_o));
  R1 r1_4 (.A(r1_3_o), .Arithmetic(Arithmetic), .Shift(decode_1_o4), .O(r1_4_o));
  R1 r1_5 (.A(r1_4_o), .Arithmetic(Arithmetic), .Shift(decode_1_o5), .O(r1_5_o));
  R1 r1_6 (.A(r1_5_o), .Arithmetic(Arithmetic), .Shift(decode_1_o6), .O(r1_6_o));
  R1 r1_7 (.A(r1_6_o), .Arithmetic(Arithmetic), .Shift(decode_1_o7), .O(O));
endmodule

module Decode (
  input  [2:0] Shift,
  output O1,
  output O2,
  output O3,
  output O4,
  output O5,
  output O6,
  output O7
);

  wire and_1_out, and_2_out, and_3_out;

  or or_1 (O1, Shift[0], Shift[1], Shift[2]);
  or or_2 (O2, Shift[1], Shift[2]);
  and and_1 (and_1_out, Shift[1], Shift[0]);
  and and_2 (and_2_out, Shift[2], Shift[0]);
  and and_3 (and_3_out, Shift[2], Shift[1]);
  and and_4 (O6, Shift[2], Shift[1]);
  and and_5 (O7, Shift[2], Shift[1], Shift[0]);
  or or_3 (O3, and_1_out, Shift[2]);
  or or_4 (O5, and_2_out, and_3_out);

  assign O4 = Shift[2];
endmodule

module Comp (
  input  A,
  input  B,
  input  I_gt,
  input  I_eq,
  input  I_lt,
  output O_gt,
  output O_eq,
  output O_lt
);

  wire and_1_out, and_2_out, not_1_out, not_2_out, xnor_1_out;

  not not_1 (not_1_out, A);
  not not_2 (not_2_out, B);
  and and_1 (and_1_out, I_eq, A, not_2_out);
  and and_2 (and_2_out, I_eq, not_1_out, B);
  or or_1 (O_gt, I_gt, and_1_out);
  xnor xnor_1 (xnor_1_out, A, B);
  or or_2 (O_lt, I_lt, and_2_out);
  and and_3 (O_eq, I_eq, xnor_1_out);
endmodule

module EightBitComparator (
  input  [7:0] A,
  input  [7:0] B,
  output GreaterThan,
  output Equal,
  output LessThan
);

  wire comp_1_o_eq, comp_1_o_gt, comp_1_o_lt, comp_2_o_eq, comp_2_o_gt, comp_2_o_lt, comp_3_o_eq,
       comp_3_o_gt, comp_3_o_lt, comp_4_o_eq, comp_4_o_gt, comp_4_o_lt, comp_5_o_eq, comp_5_o_gt,
       comp_5_o_lt, comp_6_o_eq, comp_6_o_gt, comp_6_o_lt, comp_7_o_eq, comp_7_o_gt, comp_7_o_lt;

  Comp comp_1 (
    .A(A[7]), .B(B[7]), .I_gt(1'b0), .I_eq(1'b1), .I_lt(1'b0), .O_gt(comp_1_o_gt), .O_eq(comp_1_o_eq),
    .O_lt(comp_1_o_lt));
  Comp comp_2 (
    .A(A[5]), .B(B[5]), .I_gt(comp_3_o_gt), .I_eq(comp_3_o_eq), .I_lt(comp_3_o_lt), .O_gt(comp_2_o_gt),
    .O_eq(comp_2_o_eq), .O_lt(comp_2_o_lt));
  Comp comp_3 (
    .A(A[6]), .B(B[6]), .I_gt(comp_1_o_gt), .I_eq(comp_1_o_eq), .I_lt(comp_1_o_lt), .O_gt(comp_3_o_gt),
    .O_eq(comp_3_o_eq), .O_lt(comp_3_o_lt));
  Comp comp_4 (
    .A(A[4]), .B(B[4]), .I_gt(comp_2_o_gt), .I_eq(comp_2_o_eq), .I_lt(comp_2_o_lt), .O_gt(comp_4_o_gt),
    .O_eq(comp_4_o_eq), .O_lt(comp_4_o_lt));
  Comp comp_5 (
    .A(A[3]), .B(B[3]), .I_gt(comp_4_o_gt), .I_eq(comp_4_o_eq), .I_lt(comp_4_o_lt), .O_gt(comp_5_o_gt),
    .O_eq(comp_5_o_eq), .O_lt(comp_5_o_lt));
  Comp comp_6 (
    .A(A[2]), .B(B[2]), .I_gt(comp_5_o_gt), .I_eq(comp_5_o_eq), .I_lt(comp_5_o_lt), .O_gt(comp_6_o_gt),
    .O_eq(comp_6_o_eq), .O_lt(comp_6_o_lt));
  Comp comp_7 (
    .A(A[1]), .B(B[1]), .I_gt(comp_6_o_gt), .I_eq(comp_6_o_eq), .I_lt(comp_6_o_lt), .O_gt(comp_7_o_gt),
    .O_eq(comp_7_o_eq), .O_lt(comp_7_o_lt));
  Comp comp_8 (
    .A(A[0]), .B(B[0]), .I_gt(comp_7_o_gt), .I_eq(comp_7_o_eq), .I_lt(comp_7_o_lt), .O_gt(GreaterThan),
    .O_eq(Equal), .O_lt(LessThan));
endmodule
