// Logisim project Problem3.circ as structural Verilog: 4 circuits, main circuit main
module main (
  input  Right,
  input  Left
);

  wire clock_1_out, decode_1_o_0, decode_1_o_1, decode_1_o_2, decode_1_o_3, decode_1_o_4, decode_1_o_5,
       decode_1_o_6, decode_1_o_7, decode_1_o_8, decode_1_o_9, decode_1_o_10, decode_1_o_11, decode_1_o_12,
       decode_1_o_13, decode_1_o_a, decode_1_o_b, decode_1_o_c, decode_1_o_d, decode_1_o_e, decode_1_o_f,
       or_1_out;
  wire [4:0] controlled_buffer_1_out, decrement_1_o, increment_1_o;
  wire [19:0] rom_1_data;

  Clock clock_1 (.out(clock_1_out));
  Increment increment_1 (.Active(Right), .clk(clock_1_out), .O(increment_1_o));
  Decrement decrement_1 (.Active(Left), .clk(clock_1_out), .O(decrement_1_o));
  or or_1 (or_1_out, Right, Left);
  assign controlled_buffer_1_out = Right ? increment_1_o : 5'bz;  // Controlled_Buffer controlled_buffer_1
  assign controlled_buffer_1_out = Left ? decrement_1_o : 5'bz;  // Controlled_Buffer controlled_buffer_2
  ROM #(.addrWidth(5), .dataWidth(20)) rom_1 (.addr(controlled_buffer_1_out), .data(rom_1_data));
  LED led_1 (.in(decode_1_o_0));
  LED led_2 (.in(decode_1_o_1));
  LED led_3 (.in(decode_1_o_2));
  LED led_4 (.in(decode_1_o_3));
  Decode decode_1 (
    .I(controlled_buffer_1_out), .E(or_1_out), .O_0(decode_1_o_0), .O_1(decode_1_o_1), .O_2(decode_1_o_2),
    .O_3(decode_1_o_3), .O_4(decode_1_o_4), .O_5(decode_1_o_5), .O_6(decode_1_o_6), .O_7(decode_1_o_7),
    .O_8(decode_1_o_8), .O_9(decode_1_o_9), .O_A(decode_1_o_a), .O_B(decode_1_o_b), .O_C(decode_1_o_c),
    .O_D(decode_1_o_d), .O_E(decode_1_o_e), .O_F(decode_1_o_f), .O_10(decode_1_o_10), .O_11(decode_1_o_11),
    .O_12(decode_1_o_12), .O_13(decode_1_o_13));
  LED led_5 (.in(rom_1_data[19]));
  LED led_6 (.in(rom_1_data[18]));
  LED led_7 (.in(rom_1_data[17]));
  LED led_8 (.in(rom_1_data[16]));
  LED led_9 (.in(decode_1_o_4));
  LED led_10 (.in(decode_1_o_5));
  LED led_11 (.in(decode_1_o_6));
  LED led_12 (.in(decode_1_o_7));
  LED led_13 (.in(rom_1_data[15]));
  LED led_14 (.in(rom_1_data[14]));
  LED led_15 (.in(rom_1_data[13]));
  LED led_16 (.in(rom_1_data[12]));
  LED led_17 (.in(decode_1_o_a));
  LED led_18 (.in(decode_1_o_b));
  LED led_19 (.in(decode_1_o_8));
  LED led_20 (.in(decode_1_o_9));
  LED led_21 (.in(rom_1_data[9]));
  LED led_22 (.in(rom_1_data[8]));
  LED led_23 (.in(rom_1_data[11]));
  LED led_24 (.in(rom_1_data[10]));
  LED led_25 (.in(decode_1_o_c));
  LED led_26 (.in(decode_1_o_d));
  LED led_27 (.in(decode_1_o_e));
  LED led_28 (.in(decode_1_o_f));
  LED led_29 (.in(rom_1_data[7]));
  LED led_30 (.in(rom_1_data[6]));
  LED led_31 (.in(rom_1_data[5]));
  LED led_32 (.in(rom_1_data[4]));
  LED led_33 (.in(decode_1_o_10));
  LED led_34 (.in(decode_1_o_11));
  LED led_35 (.in(decode_1_o_12));
  LED led_36 (.in(decode_1_o_13));
  LED led_37 (.in(rom_1_data[3]));
  LED led_38 (.in(rom_1_data[2]));
  LED led_39 (.in(rom_1_data[1]));
  LED led_40 (.in(rom_1_data[0]));

  // Notes on the sheet:
  //   contents of rom_1 (hex, n*v repeats v):
  //   80000 40000 20000 10000 8000 4000 2000 1000 800 400 200 100 80 40 20 10 8 4 2 1
endmodule

module Increment (
  input  Active,
  input  clk,
  output [4:0] O
);

  wire comparator_1_eq;
  wire [4:0] adder_1_out;

  Adder #(.width(5)) adder_1 (.a(O), .b(5'b00001), .out(adder_1_out));  // open: cin, cout
  Register #(.width(5)) register_1 (.D(adder_1_out), .en(Active), .clk(clk), .Q(O), .clr(comparator_1_eq));
  Comparator #(.width(5)) comparator_1 (.a(O), .b(5'b10100), .eq(comparator_1_eq));  // open: gt, lt
endmodule

module Decrement (
  input  Active,
  input  clk,
  output [4:0] O
);

  wire comparator_1_eq;
  wire [4:0] adder_1_out, not_1_out, register_1_q;

  Adder #(.width(5)) adder_1 (.a(register_1_q), .b(5'b00001), .out(adder_1_out));  // open: cin, cout
  Register #(.width(5)) register_1 (.D(adder_1_out), .en(Active), .clk(clk), .Q(register_1_q), .clr(comparator_1_eq));
  assign not_1_out = ~register_1_q;  // NOT_Gate not_1, 5 bits wide
  Adder #(.width(5)) adder_2 (.a(not_1_out), .b(5'b10100), .out(O));  // open: cin, cout
  Comparator #(.width(5)) comparator_1 (.a(register_1_q), .b(5'b10100), .eq(comparator_1_eq));  // open: gt, lt
endmodule

module Decode (
  input  [4:0] I,
  input  E,
  output O_0,
  output O_1,
  output O_2,
  output O_3,
  output O_4,
  output O_5,
  output O_6,
  output O_7,
  output O_8,
  output O_9,
  output O_A,
  output O_B,
  output O_C,
  output O_D,
  output O_E,
  output O_F,
  output O_10,
  output O_11,
  output O_12,
  output O_13
);

  wire not_1_out, not_2_out, not_3_out, not_4_out, not_5_out;

  not not_1 (not_1_out, I[4]);
  not not_2 (not_2_out, I[3]);
  not not_3 (not_3_out, I[2]);
  not not_4 (not_4_out, I[1]);
  not not_5 (not_5_out, I[0]);
  and and_1 (O_0, not_1_out, not_2_out, not_3_out, not_4_out, not_5_out, E);
  and and_2 (O_1, not_1_out, not_2_out, not_3_out, not_4_out, I[0], E);
  and and_3 (O_2, not_1_out, not_2_out, not_3_out, I[1], not_5_out, E);
  and and_4 (O_3, not_1_out, not_2_out, not_3_out, I[1], I[0], E);
  and and_5 (O_4, not_1_out, not_2_out, I[2], not_4_out, not_5_out, E);
  and and_6 (O_5, not_1_out, not_2_out, I[2], not_4_out, I[0], E);
  and and_7 (O_6, not_1_out, not_2_out, I[2], I[1], not_5_out, E);
  and and_8 (O_7, not_1_out, not_2_out, I[2], I[1], I[0], E);
  and and_9 (O_8, not_1_out, I[3], not_3_out, not_4_out, not_5_out, E);
  and and_10 (O_9, not_1_out, I[3], not_3_out, not_4_out, I[0], E);
  and and_11 (O_A, not_1_out, I[3], not_3_out, I[1], not_5_out, E);
  and and_12 (O_B, not_1_out, I[3], not_3_out, I[1], I[0], E);
  and and_13 (O_C, not_1_out, I[3], I[2], not_4_out, not_5_out, E);
  and and_14 (O_D, not_1_out, I[3], I[2], not_4_out, I[0], E);
  and and_15 (O_E, not_1_out, I[3], I[2], I[1], not_5_out, E);
  and and_16 (O_F, not_1_out, I[3], I[2], I[1], I[0], E);
  and and_17 (O_10, I[4], not_2_out, not_3_out, not_4_out, not_5_out, E);
  and and_18 (O_11, I[4], not_2_out, not_3_out, not_4_out, I[0], E);
  and and_19 (O_12, I[4], not_2_out, not_3_out, I[1], not_5_out, E);
  and and_20 (O_13, I[4], not_2_out, not_3_out, I[1], I[0], E);
endmodule
